// Logisim project ProjetoCircuitosFinal1.circ as structural Verilog: 20 circuits, main circuit main
module main (
  input  [1:0] SelA,
  input  [2:0] SelOperacao,
  input  [1:0] SelB,
  input  [7:0] InsereValor,
  input  Sel,
  input  [1:0] in_6,
  output [7:0] out_7
);

  wire Escrever_out, ula_1_overflowc, ula_1_z;
  wire [7:0] meio_1_sa, meio_1_sb, mux8bits2x1_1_saida;

  Button Escrever (.out(Escrever_out));
  Mux8bits2x1 mux8bits2x1_1 (.EntradaA(out_7), .EntradaB(InsereValor), .Selecao(Sel), .Saida(mux8bits2x1_1_saida));
  Meio meio_1 (
    .RA(SelA), .RB(SelB), .Entrada(mux8bits2x1_1_saida), .Clock(Escrever_out), .Sel(in_6), .SA(meio_1_sa),
    .SB(meio_1_sb));
  ULA ula_1 (
    .A(meio_1_sa), .SelecaoOperacao(SelOperacao), .B(meio_1_sb), .Resultado(out_7), .Z(ula_1_z),
    .OverflowC(ula_1_overflowc));
  LED Zero (.in(ula_1_z));
  LED Overflow (.in(ula_1_overflowc));

  // Notes on the sheet:
  //   y=2*4+(-1)
  //   y=2(3)^2+4(3)+(-1) = 29
  //   y=2*3+(-1)
  //   y=2(2)^2+4(2)+(-1) = 15
  //   000 AnandB
  //   001 A*B
  //   010 A-B
  //   011 AxorB
  //   100 AandB
  //   101 A/B
  //   110 AorB
  //   111 A+B
  //   Bruno Schramm Vendruscolo
  //   R00 = 2
  //   R01 =4
  //   R10= 3
  //   R11
endmodule

module Mux2x1 (
  input  [1:0] Entrada,
  input  Sel,
  output out_3
);

  wire and_1_out, and_2_out, not_1_out;

  and and_1 (and_1_out, Entrada[0], not_1_out);
  not not_1 (not_1_out, Sel);
  and and_2 (and_2_out, Entrada[1], Sel);
  or or_1 (out_3, and_1_out, and_2_out);
endmodule

module Somador (
  input  c,
  input  a,
  input  b,
  output Resultado,
  output Carry
);

  wire and_1_out, and_2_out, and_3_out, xor_1_out;

  xor xor_1 (xor_1_out, b, c);
  and and_1 (and_1_out, a, b);
  and and_2 (and_2_out, a, c);
  and and_3 (and_3_out, b, c);
  xor xor_2 (Resultado, xor_1_out, a);
  or or_1 (Carry, and_1_out, and_2_out, and_3_out);
endmodule

module RegistradorJK (
  input  EntradaSerial,
  input  Clock,
  output SaidaSerial
);

  wire j_k_ff_1_q, j_k_ff_1_qn, j_k_ff_2_q, j_k_ff_2_qn, j_k_ff_3_q, j_k_ff_3_qn, j_k_ff_4_q, j_k_ff_4_qn,
       j_k_ff_5_q, j_k_ff_5_qn, j_k_ff_6_q, j_k_ff_6_qn, j_k_ff_7_q, j_k_ff_7_qn, not_1_out;

  J_K_Flip_Flop j_k_ff_1 (
    .J(EntradaSerial), .K(not_1_out), .clk(Clock), .Q(j_k_ff_1_q), .Qn(j_k_ff_1_qn));  // open: preset, reset
  not not_1 (not_1_out, EntradaSerial);
  J_K_Flip_Flop j_k_ff_2 (
    .J(j_k_ff_1_q), .K(j_k_ff_1_qn), .clk(Clock), .Q(j_k_ff_2_q), .Qn(j_k_ff_2_qn));  // open: preset, reset
  J_K_Flip_Flop j_k_ff_3 (
    .J(j_k_ff_2_q), .K(j_k_ff_2_qn), .clk(Clock), .Q(j_k_ff_3_q), .Qn(j_k_ff_3_qn));  // open: preset, reset
  J_K_Flip_Flop j_k_ff_4 (
    .J(j_k_ff_3_q), .K(j_k_ff_3_qn), .clk(Clock), .Q(j_k_ff_4_q), .Qn(j_k_ff_4_qn));  // open: preset, reset
  J_K_Flip_Flop j_k_ff_5 (
    .J(j_k_ff_4_q), .K(j_k_ff_4_qn), .clk(Clock), .Q(j_k_ff_5_q), .Qn(j_k_ff_5_qn));  // open: preset, reset
  J_K_Flip_Flop j_k_ff_6 (
    .J(j_k_ff_5_q), .K(j_k_ff_5_qn), .clk(Clock), .Q(j_k_ff_6_q), .Qn(j_k_ff_6_qn));  // open: preset, reset
  J_K_Flip_Flop j_k_ff_7 (
    .J(j_k_ff_6_q), .K(j_k_ff_6_qn), .clk(Clock), .Q(j_k_ff_7_q), .Qn(j_k_ff_7_qn));  // open: preset, reset
  J_K_Flip_Flop j_k_ff_8 (.J(j_k_ff_7_q), .K(j_k_ff_7_qn), .clk(Clock), .Q(SaidaSerial));  // open: Qn, preset, reset
endmodule

module Registradores (
  input  [7:0] Entrada,
  input  Clock,
  output [7:0] Saida
);

  D_Flip_Flop d_ff_1 (.D(Entrada[0]), .clk(Clock), .Q(Saida[0]));  // open: Qn, preset, reset
  D_Flip_Flop d_ff_2 (.D(Entrada[1]), .clk(Clock), .Q(Saida[1]));  // open: Qn, preset, reset
  D_Flip_Flop d_ff_3 (.D(Entrada[2]), .clk(Clock), .Q(Saida[2]));  // open: Qn, preset, reset
  D_Flip_Flop d_ff_4 (.D(Entrada[3]), .clk(Clock), .Q(Saida[3]));  // open: Qn, preset, reset
  D_Flip_Flop d_ff_5 (.D(Entrada[4]), .clk(Clock), .Q(Saida[4]));  // open: Qn, preset, reset
  D_Flip_Flop d_ff_6 (.D(Entrada[5]), .clk(Clock), .Q(Saida[5]));  // open: Qn, preset, reset
  D_Flip_Flop d_ff_7 (.D(Entrada[6]), .clk(Clock), .Q(Saida[6]));  // open: Qn, preset, reset
  D_Flip_Flop d_ff_8 (.D(Entrada[7]), .clk(Clock), .Q(Saida[7]));  // open: Qn, preset, reset
endmodule

module Mux4x1 (
  input  [1:0] in_1,
  input  [3:0] Entrada,
  output out_3
);

  wire and_1_out, and_2_out, and_3_out, and_4_out, not_1_out, not_2_out, not_3_out, not_4_out;

  not not_1 (not_1_out, in_1[1]);
  not not_2 (not_2_out, in_1[0]);
  and and_1 (and_1_out, not_1_out, not_2_out, Entrada[0]);
  not not_3 (not_3_out, in_1[1]);
  and and_2 (and_2_out, not_3_out, in_1[0], Entrada[1]);
  not not_4 (not_4_out, in_1[0]);
  and and_3 (and_3_out, not_4_out, in_1[1], Entrada[2]);
  and and_4 (and_4_out, Entrada[3], in_1[1], in_1[0]);
  or or_1 (out_3, and_2_out, and_1_out, and_3_out, and_4_out);
endmodule

module SomarSubtrair (
  input  Subtrair,
  input  [7:0] A,
  input  [7:0] B,
  output [7:0] Resultado,
  output Overflow
);

  wire somador_1_carry, somador_2_carry, somador_3_carry, somador_4_carry, somador_5_carry, somador_6_carry,
       somador_7_carry, xor_1_out, xor_2_out, xor_3_out, xor_4_out, xor_5_out, xor_6_out, xor_7_out,
       xor_8_out;

  xor xor_1 (xor_1_out, B[0], Subtrair);
  xor xor_2 (xor_2_out, B[1], Subtrair);
  xor xor_3 (xor_3_out, B[2], Subtrair);
  xor xor_4 (xor_4_out, B[3], Subtrair);
  xor xor_5 (xor_5_out, B[4], Subtrair);
  xor xor_6 (xor_6_out, B[5], Subtrair);
  xor xor_7 (xor_7_out, B[6], Subtrair);
  xor xor_8 (xor_8_out, B[7], Subtrair);
  Somador somador_1 (.c(Subtrair), .a(A[0]), .b(xor_1_out), .Resultado(Resultado[0]), .Carry(somador_1_carry));
  Somador somador_2 (.c(somador_1_carry), .a(A[1]), .b(xor_2_out), .Resultado(Resultado[1]), .Carry(somador_2_carry));
  Somador somador_3 (.c(somador_2_carry), .a(A[2]), .b(xor_3_out), .Resultado(Resultado[2]), .Carry(somador_3_carry));
  Somador somador_4 (.c(somador_3_carry), .a(A[3]), .b(xor_4_out), .Resultado(Resultado[3]), .Carry(somador_4_carry));
  Somador somador_5 (.c(somador_4_carry), .a(A[4]), .b(xor_5_out), .Resultado(Resultado[4]), .Carry(somador_5_carry));
  Somador somador_6 (.c(somador_5_carry), .a(A[5]), .b(xor_6_out), .Resultado(Resultado[5]), .Carry(somador_6_carry));
  Somador somador_7 (.c(somador_6_carry), .a(A[6]), .b(xor_7_out), .Resultado(Resultado[6]), .Carry(somador_7_carry));
  Somador somador_8 (.c(somador_7_carry), .a(A[7]), .b(xor_8_out), .Resultado(Resultado[7]), .Carry(Overflow));
endmodule

module Mux8x1 (
  input  [7:0] Entrada,
  input  [2:0] Selecao,
  output Saida
);

  wire and_1_out, and_2_out, and_3_out, and_4_out, and_5_out, and_6_out, and_7_out, and_8_out;

  and and_1 (and_1_out, ~Selecao[0], ~Selecao[1], ~Selecao[2], Entrada[0]);  // AND_Gate
  and and_2 (and_2_out, ~Selecao[2], ~Selecao[1], Selecao[0], Entrada[1]);  // AND_Gate
  and and_3 (and_3_out, ~Selecao[2], Selecao[1], ~Selecao[0], Entrada[2]);  // AND_Gate
  and and_4 (and_4_out, ~Selecao[2], Selecao[1], Selecao[0], Entrada[3]);  // AND_Gate
  and and_5 (and_5_out, Selecao[2], ~Selecao[1], ~Selecao[0], Entrada[4]);  // AND_Gate
  and and_6 (and_6_out, Selecao[2], ~Selecao[1], Selecao[0], Entrada[5]);  // AND_Gate
  and and_7 (and_7_out, Selecao[2], Selecao[1], ~Selecao[0], Entrada[6]);  // AND_Gate
  and and_8 (and_8_out, Selecao[0], Selecao[1], Selecao[2], Entrada[7]);
  or or_1 (Saida, and_8_out, and_7_out, and_6_out, and_5_out, and_4_out, and_3_out, and_2_out, and_1_out);
endmodule

module Mux8bits4x1 (
  input  [7:0] Entrada0,
  input  [7:0] Entrada1,
  input  [7:0] Entrada2,
  input  [7:0] Entrada3,
  input  [1:0] Selecao,
  output [7:0] Saida
);

  Mux4x1 mux4x1_1 (.in_1(Selecao), .Entrada({Entrada3[0], Entrada2[0], Entrada1[0], Entrada0[0]}), .out_3(Saida[0]));
  Mux4x1 mux4x1_2 (.in_1(Selecao), .Entrada({Entrada3[1], Entrada2[1], Entrada1[1], Entrada0[1]}), .out_3(Saida[1]));
  Mux4x1 mux4x1_3 (.in_1(Selecao), .Entrada({Entrada3[2], Entrada2[2], Entrada1[2], Entrada0[2]}), .out_3(Saida[2]));
  Mux4x1 mux4x1_4 (.in_1(Selecao), .Entrada({Entrada3[3], Entrada2[3], Entrada1[3], Entrada0[3]}), .out_3(Saida[3]));
  Mux4x1 mux4x1_5 (.in_1(Selecao), .Entrada({Entrada3[4], Entrada2[4], Entrada1[4], Entrada0[4]}), .out_3(Saida[4]));
  Mux4x1 mux4x1_6 (.in_1(Selecao), .Entrada({Entrada3[5], Entrada2[5], Entrada1[5], Entrada0[5]}), .out_3(Saida[5]));
  Mux4x1 mux4x1_7 (.in_1(Selecao), .Entrada({Entrada3[6], Entrada2[6], Entrada1[6], Entrada0[6]}), .out_3(Saida[6]));
  Mux4x1 mux4x1_8 (.in_1(Selecao), .Entrada({Entrada3[7], Entrada2[7], Entrada1[7], Entrada0[7]}), .out_3(Saida[7]));
endmodule

module Mux8bits2x1 (
  input  [7:0] EntradaA,
  input  [7:0] EntradaB,
  input  Selecao,
  output [7:0] Saida
);

  Mux2x1 mux2x1_1 (.Entrada({EntradaB[0], EntradaA[0]}), .Sel(Selecao), .out_3(Saida[0]));
  Mux2x1 mux2x1_2 (.Entrada({EntradaB[1], EntradaA[1]}), .Sel(Selecao), .out_3(Saida[1]));
  Mux2x1 mux2x1_3 (.Entrada({EntradaB[2], EntradaA[2]}), .Sel(Selecao), .out_3(Saida[2]));
  Mux2x1 mux2x1_4 (.Entrada({EntradaB[3], EntradaA[3]}), .Sel(Selecao), .out_3(Saida[3]));
  Mux2x1 mux2x1_5 (.Entrada({EntradaB[4], EntradaA[4]}), .Sel(Selecao), .out_3(Saida[4]));
  Mux2x1 mux2x1_6 (.Entrada({EntradaB[5], EntradaA[5]}), .Sel(Selecao), .out_3(Saida[5]));
  Mux2x1 mux2x1_7 (.Entrada({EntradaB[6], EntradaA[6]}), .Sel(Selecao), .out_3(Saida[6]));
  Mux2x1 mux2x1_8 (.Entrada({EntradaB[7], EntradaA[7]}), .Sel(Selecao), .out_3(Saida[7]));
endmodule

module Mux8bits8x1 (
  input  [2:0] Selecao,
  input  [7:0] Entrada0,
  input  [7:0] Entrada1,
  input  [7:0] Entrada2,
  input  [7:0] Entrada3,
  input  [7:0] Entrada4,
  input  [7:0] Entrada5,
  input  [7:0] Entrada6,
  input  [7:0] Entrada7,
  output [7:0] out_10
);

  Mux8x1 mux8x1_1 (
    .Entrada({Entrada7[7], Entrada6[7], Entrada5[7], Entrada4[7], Entrada3[7], Entrada2[7], Entrada1[7], Entrada0[7]}),
    .Selecao(Selecao), .Saida(out_10[7]));
  Mux8x1 mux8x1_2 (
    .Entrada({Entrada7[6], Entrada6[6], Entrada5[6], Entrada4[6], Entrada3[6], Entrada2[6], Entrada1[6], Entrada0[6]}),
    .Selecao(Selecao), .Saida(out_10[6]));
  Mux8x1 mux8x1_3 (
    .Entrada({Entrada7[5], Entrada6[5], Entrada5[5], Entrada4[5], Entrada3[5], Entrada2[5], Entrada1[5], Entrada0[5]}),
    .Selecao(Selecao), .Saida(out_10[5]));
  Mux8x1 mux8x1_4 (
    .Entrada({Entrada7[4], Entrada6[4], Entrada5[4], Entrada4[4], Entrada3[4], Entrada2[4], Entrada1[4], Entrada0[4]}),
    .Selecao(Selecao), .Saida(out_10[4]));
  Mux8x1 mux8x1_5 (
    .Entrada({Entrada7[3], Entrada6[3], Entrada5[3], Entrada4[3], Entrada3[3], Entrada2[3], Entrada1[3], Entrada0[3]}),
    .Selecao(Selecao), .Saida(out_10[3]));
  Mux8x1 mux8x1_6 (
    .Entrada({Entrada7[2], Entrada6[2], Entrada5[2], Entrada4[2], Entrada3[2], Entrada2[2], Entrada1[2], Entrada0[2]}),
    .Selecao(Selecao), .Saida(out_10[2]));
  Mux8x1 mux8x1_7 (
    .Entrada({Entrada7[1], Entrada6[1], Entrada5[1], Entrada4[1], Entrada3[1], Entrada2[1], Entrada1[1], Entrada0[1]}),
    .Selecao(Selecao), .Saida(out_10[1]));
  Mux8x1 mux8x1_8 (
    .Entrada({Entrada7[0], Entrada6[0], Entrada5[0], Entrada4[0], Entrada3[0], Entrada2[0], Entrada1[0], Entrada0[0]}),
    .Selecao(Selecao), .Saida(out_10[0]));
endmodule

module Meio (
  input  [1:0] RA,
  input  [1:0] RB,
  input  [7:0] Entrada,
  input  Clock,
  input  [1:0] Sel,
  output [7:0] SA,
  output [7:0] SB
);

  wire demux2x1_1_s0, demux2x1_1_s1, demux2x1_1_s2, demux2x1_1_s3;
  wire [7:0] registradores_1_saida, registradores_2_saida, registradores_3_saida, registradores_4_saida;

  Demux2x1 demux2x1_1 (
    .Entrada(Clock), .Sel(Sel), .S0(demux2x1_1_s0), .S1(demux2x1_1_s1), .S2(demux2x1_1_s2), .S3(demux2x1_1_s3));
  Registradores registradores_1 (.Entrada(Entrada), .Clock(demux2x1_1_s0), .Saida(registradores_1_saida));
  Registradores registradores_2 (.Entrada(Entrada), .Clock(demux2x1_1_s1), .Saida(registradores_2_saida));
  Registradores registradores_3 (.Entrada(Entrada), .Clock(demux2x1_1_s2), .Saida(registradores_3_saida));
  Registradores registradores_4 (.Entrada(Entrada), .Clock(demux2x1_1_s3), .Saida(registradores_4_saida));
  Mux8bits4x1 mux8bits4x1_1 (
    .Entrada0(registradores_1_saida), .Entrada1(registradores_2_saida), .Entrada2(registradores_3_saida),
    .Entrada3(registradores_4_saida), .Selecao(RA), .Saida(SA));
  Mux8bits4x1 mux8bits4x1_2 (
    .Entrada0(registradores_1_saida), .Entrada1(registradores_2_saida), .Entrada2(registradores_3_saida),
    .Entrada3(registradores_4_saida), .Selecao(RB), .Saida(SB));
endmodule

module Demux2x1 (
  input  Entrada,
  input  [1:0] Sel,
  output S0,
  output S1,
  output S2,
  output S3
);

  and and_1 (S0, ~Sel[1], ~Sel[0], Entrada);  // AND_Gate
  and and_2 (S1, ~Sel[1], Sel[0], Entrada);  // AND_Gate
  and and_3 (S2, Sel[1], ~Sel[0], Entrada);  // AND_Gate
  and and_4 (S3, Sel[1], Sel[0], Entrada);
endmodule

module ULA (
  input  [7:0] A,
  input  [2:0] SelecaoOperacao,
  input  [7:0] B,
  output [7:0] Resultado,
  output Z,
  output OverflowC
);

  wire or_1_out, or_2_out, somarsubtrair_1_overflow, somarsubtrair_2_overflow;
  wire [7:0] aandb_1_out_3, aandb_2_out_3, aorb_1_out_3, axorb_1_out_3, divider_1_out, divider_1_rem,
       multiplier_1_cout, multiplier_1_out, not_1_out, somarsubtrair_1_resultado, somarsubtrair_2_resultado;

  Multiplier multiplier_1 (.a(A), .b(B), .out(multiplier_1_out), .cout(multiplier_1_cout));  // open: cin
  Divider divider_1 (.a(A), .b(B), .out(divider_1_out), .rem(divider_1_rem));  // open: upper
  AandB aandb_1 (.A(A), .B(B), .out_3(aandb_1_out_3));
  SomarSubtrair somarsubtrair_1 (
    .Subtrair(1'b1), .A(A), .B(B), .Resultado(somarsubtrair_1_resultado), .Overflow(somarsubtrair_1_overflow));
  AxorB axorb_1 (.EntradaA(A), .EntradaB(B), .out_3(axorb_1_out_3));
  AandB aandb_2 (.A(A), .B(B), .out_3(aandb_2_out_3));
  AorB aorb_1 (.A(A), .B(B), .out_3(aorb_1_out_3));
  SomarSubtrair somarsubtrair_2 (
    .Subtrair(1'b0), .A(A), .B(B), .Resultado(somarsubtrair_2_resultado), .Overflow(somarsubtrair_2_overflow));
  assign not_1_out = ~aandb_1_out_3;  // NOT_Gate not_1, 8 bits wide
  or or_1 (or_1_out, multiplier_1_cout[0], multiplier_1_cout[1], multiplier_1_cout[2], multiplier_1_cout[3], multiplier_1_cout[4], multiplier_1_cout[5], multiplier_1_cout[6], multiplier_1_cout[7]);
  or or_2 (or_2_out, divider_1_rem[0], divider_1_rem[1], divider_1_rem[2], divider_1_rem[3], divider_1_rem[4], divider_1_rem[5], divider_1_rem[6], divider_1_rem[7]);
  Mux8bits8x1 mux8bits8x1_1 (
    .Selecao(SelecaoOperacao), .Entrada0(not_1_out), .Entrada1(multiplier_1_out),
    .Entrada2(somarsubtrair_1_resultado), .Entrada3(axorb_1_out_3), .Entrada4(aandb_2_out_3),
    .Entrada5(divider_1_out), .Entrada6(aorb_1_out_3), .Entrada7(somarsubtrair_2_resultado),
    .out_10(Resultado));
  Mux8x1bits mux8x1bits_1 (
    .E00(1'b0), .E01(or_1_out), .E10(somarsubtrair_1_overflow), .E11(1'b0), .E100(1'b0), .E101(or_2_out),
    .E110(1'b0), .Selecao(SelecaoOperacao), .E111(somarsubtrair_2_overflow), .Saida(OverflowC));
  Zero zero_1 (.Entrada(Resultado), .Saida(Z));
endmodule

module AandB (
  input  [7:0] A,
  input  [7:0] B,
  output [7:0] out_3
);

  assign out_3 = A & B;  // AND_Gate and_1, 8 bits wide
endmodule

module AxorB (
  input  [7:0] EntradaA,
  input  [7:0] EntradaB,
  output [7:0] out_3
);

  assign out_3 = EntradaA ^ EntradaB;  // XOR_Gate xor_1, 8 bits wide
endmodule

module AorB (
  input  [7:0] A,
  input  [7:0] B,
  output [7:0] out_3
);

  assign out_3 = A | B;  // OR_Gate or_1, 8 bits wide
endmodule

module Zero (
  input  [7:0] Entrada,
  output Saida
);

  and and_1 (Saida, ~Entrada[7], ~Entrada[6], ~Entrada[5], ~Entrada[4], ~Entrada[3], ~Entrada[2], ~Entrada[1], ~Entrada[0]);  // AND_Gate
endmodule

module Mux4x13bits (
  input  [1:0] Sel,
  input  E01,
  input  E10,
  input  E11,
  input  E00,
  output out_6
);

  wire and_1_out, and_2_out, and_3_out, and_4_out, not_1_out, not_2_out, not_3_out, not_4_out;

  not not_1 (not_1_out, Sel[1]);
  not not_2 (not_2_out, Sel[0]);
  and and_1 (and_1_out, not_1_out, not_2_out, E00);
  not not_3 (not_3_out, Sel[1]);
  and and_2 (and_2_out, not_3_out, Sel[0], E01);
  not not_4 (not_4_out, Sel[0]);
  and and_3 (and_3_out, not_4_out, Sel[1], E10);
  and and_4 (and_4_out, E11, Sel[1], Sel[0]);
  or or_1 (out_6, and_2_out, and_1_out, and_3_out, and_4_out);
endmodule

module Mux8x1bits (
  input  E00,
  input  E01,
  input  E10,
  input  E11,
  input  E100,
  input  E101,
  input  E110,
  input  [2:0] Selecao,
  input  E111,
  output Saida
);

  wire and_1_out, and_2_out, and_3_out, and_4_out, and_5_out, and_6_out, and_7_out, and_8_out;

  and and_1 (and_1_out, ~Selecao[0], ~Selecao[1], ~Selecao[2], E00);  // AND_Gate
  and and_2 (and_2_out, ~Selecao[2], ~Selecao[1], Selecao[0], E01);  // AND_Gate
  and and_3 (and_3_out, ~Selecao[2], Selecao[1], ~Selecao[0], E10);  // AND_Gate
  and and_4 (and_4_out, ~Selecao[2], Selecao[1], Selecao[0], E11);  // AND_Gate
  and and_5 (and_5_out, Selecao[2], ~Selecao[1], ~Selecao[0], E100);  // AND_Gate
  and and_6 (and_6_out, Selecao[2], ~Selecao[1], Selecao[0], E101);  // AND_Gate
  and and_7 (and_7_out, Selecao[2], Selecao[1], ~Selecao[0], E110);  // AND_Gate
  and and_8 (and_8_out, Selecao[0], Selecao[1], Selecao[2], E111);
  or or_1 (Saida, and_8_out, and_7_out, and_6_out, and_5_out, and_4_out, and_3_out, and_2_out, and_1_out);
endmodule
